# Fritzing sketch circuit_diagram (saved by Fritzing 0.9.4)
breadboards: 1

parts:
  Part2 = Adafruit 1.44 inch TFT Breakout [part_number="Adafruit #2088"]
  Part3 = Adafruit ItsyBitsy M4 [part_number="Adafruit #3800"]
  KEYPAD1 = Membrane Matrix Keypad
  Part5 = Arduino Uno (Rev3)-TopMount
  J1 = Piezo Speaker
  M1 = Dagu DGServo 9g (End View) [part_number=RS001B]
  M2 = Dagu DGServo 9g (End View) [part_number=RS001B]
  M3 = Dagu DGServo 9g (End View) [part_number=RS001B]
  R1 = Resistor [tolerance=±5% resistance=1k package="0402 [SMD]"]
  R2 = Resistor [tolerance=±5% resistance=1k package="0402 [SMD]"]
  R3 = Resistor [tolerance=±5% resistance=1k package="0402 [SMD]"]
  R4 = Resistor [tolerance=±5% resistance=1k package="0402 [SMD]"]
  R5 = Resistor [tolerance=±5% resistance=100k package="0402 [SMD]"]
  R6 = Resistor [tolerance=±5% resistance=100k package="0402 [SMD]"]
  R7 = Resistor [tolerance=±5% resistance=100k package="0402 [SMD]"]
  M4 = Dagu DGServo 9g (End View) [part_number=RS001B]
  Part6 = Arduino Nano (Rev3.0)

nets:
  VCC: Part2.+3V3, Part3.+3V3, M1.vcc, M2.vcc, M3.vcc, M4.vcc
  GND: Part2.GND, Part3.GND, Part5.GND, M1.gnd, M2.gnd, M3.gnd, R1.Pin_0, R2.Pin_1, R3.Pin_1, R4.Pin_1, R5.Pin_1, R6.Pin_1, R7.Pin_1, M4.gnd, Part6.GND
  N1: Part2.SCK, Part3.SCK
  N2: Part2.MISO, Part3.MISO
  N3: Part2.MOSI, Part3.MOSI
  N4: Part2.TFTCS, Part3.D5_5V
  N5: Part2.RESET, Part3.D9
  N6: Part2.TFTDC, Part3.D7
  N7: Part3.VBUS, Part5.5V
  N8: Part3.D13, M1.pulse
  N9: Part3.D12, M2.pulse
  N10: Part3.D11, M3.pulse
  N11: Part3.A4, Part5.D3_PWM, R5.Pin_0, Part6.D4
  N12: Part3.A3, Part5.D4, R7.Pin_0, Part6.D3
  N13: Part3.A2, Part5.D2, R6.Pin_0, Part6.D2
  N14: Part3.A1, M4.pulse
  N15: KEYPAD1.1, Part5.D7
  N16: KEYPAD1.2, Part5.D8
  N17: KEYPAD1.3, Part5.D9_PWM
  N18: KEYPAD1.4, Part5.D10_PWM/SS
  N19: KEYPAD1.5, Part5.D11_PWM/MOSI, R2.Pin_0
  N20: KEYPAD1.6, Part5.D13/SCK, R4.Pin_0
  N21: KEYPAD1.7, Part5.D12/MISO, R3.Pin_0
  N22: Part5.D6_PWM, J1.pin2, Part6.D10
  N23: J1.pin1, R1.Pin_1

custom parts:
  Adafruit 1.44 inch TFT Breakout: This lovely little display breakout is the best way to add a small, colorful and bright display to any project. Since the display uses 4-wire SPI to communicate and has its own pixel-addressable frame buffer, it can be used with every kind of microcontroller. Even a very small one with low memory and few pins available! The 1.44" display has 128x128 color pixels. Unlike the low cost "Nokia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
  Adafruit ItsyBitsy M4: What's smaller than a Feather but larger than a Trinket? It's an Adafruit ItsyBitsy M4 Express featuring the Microchip ATSAMD51! Small, powerful, with a ultra fast ATSAMD51 Cortex M4 processor running at 120 MHz - this microcontroller board is perfect when you want something very compact, with a ton of horsepower and a bunch of pins. This Itsy is like a bullet train, with it's 120MHz Cortex M4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
  Membrane Matrix Keypad: Membrane Matrix 3x4 Keypad
  Arduino Uno (Rev3)-TopMount: Arduino Uno (Rev3) for Top PCB Mount. The PCB view of the Arduino Uno (Rev3) in Arduino Bin flipped upside down with the text flipped back so as to be readable. Other views haven't changed Protruding component position is outlined to provide indication of part contact. Number in component outline is mm of protrusion of the component from the UNO PCB. Subtract the number from the USB (11mm),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
